// Logisim project BiClock.circ as structural Verilog: 2 circuits, main circuit BiClock
module BiClock (
  input  reset,
  output signal0,
  output signal1
);

  wire and_1_out, horloge_out, not_1_out, register_1_q;

  not not_1 (not_1_out, register_1_q);
  Clock horloge (.out(horloge_out));
  Register #(.width(1), .trigger("falling")) register_1 (
    .D(not_1_out), .Q(register_1_q), .clk(horloge_out), .clr(reset));  // open: en
  and and_1 (and_1_out, horloge_out, ~reset);  // AND_Gate
  and and_2 (signal0, ~register_1_q, and_1_out);  // AND_Gate
  and and_3 (signal1, register_1_q, and_1_out);

  // Notes on the sheet:
  //   registre 1-bit
endmodule

module BiClock_Test (
);

  wire biclock_1_signal0, biclock_1_signal1, reset_out;

  Button reset (.out(reset_out));
  BiClock biclock_1 (.reset(reset_out), .signal0(biclock_1_signal0), .signal1(biclock_1_signal1));
  // Probe on biclock_1_signal0
  // Probe on biclock_1_signal1
endmodule
